// Logisim project Flag.circ as structural Verilog: 1 circuit, main circuit Flag Finder
module Flag_Finder (
  input  Result__0,
  input  Underflow,
  input  Overflow,
  input  [31:0] Significand,
  input  [8:0] Exponent,
  output Denormalized,
  output Underflow_2,
  output Overflow_2,
  output NaN,
  output INF
);

  wire and_1_out, n0_checker_1_p2, n1_cheacker_1_p2, n32bit_0_checker_1_p2, not_1_out, not_2_out, not_3_out,
       not_4_out;

  // _32bit_0_checker 32bit_0_checker_1: pin names not known; wires that end beside it: Significand, n32bit_0_checker_1_p2
  // _0_checker 0_checker_1: pin names not known; wires that end beside it: Exponent, n0_checker_1_p2
  // _1_cheacker 1_cheacker_1: pin names not known; wires that end beside it: Exponent, n1_cheacker_1_p2
  not not_1 (not_1_out, n32bit_0_checker_1_p2);
  not not_2 (not_2_out, Result__0);
  not not_3 (not_3_out, Underflow);
  and and_1 (and_1_out, not_3_out, not_4_out);
  not not_4 (not_4_out, Overflow);
  and and_2 (NaN, not_1_out, and_1_out, n1_cheacker_1_p2);
  and and_3 (INF, n32bit_0_checker_1_p2, and_1_out, n1_cheacker_1_p2);
  and and_4 (Denormalized, not_2_out, n0_checker_1_p2, and_1_out);

  assign Overflow_2 = Overflow;
  assign Underflow_2 = Underflow;
endmodule
